// Logisim project Relogio.circ as structural Verilog: 2 circuits, main circuit main
module main (
  input  in_1
);

  _7_Segment_Display u_7_segment_display_1 ();  // open: g, f, a, b, e, d, c, dp
  Contador0_9 contador0_9_1 ();  // open: out_6, out_3, out_4, Clock, out_5, Reset
endmodule

module Contador0_9 (
  input  Reset,
  input  Clock,
  output out_3,
  output out_4,
  output out_5,
  output out_6
);

  wire and_1_out, and_2_out, and_3_out, and_4_out, or_1_out;

  J_K_Flip_Flop j_k_ff_1 (.J(1'b1), .clk(Clock), .K(1'b1), .Q(out_5), .reset(or_1_out));  // open: Qn, preset, en
  and and_1 (and_1_out, out_6, out_4);
  J_K_Flip_Flop j_k_ff_2 (.J(out_5), .clk(Clock), .K(out_5), .Q(out_6), .reset(or_1_out));  // open: Qn, preset, en
  and and_2 (and_2_out, out_5, out_6);
  and and_3 (and_3_out, and_2_out, out_3);
  J_K_Flip_Flop j_k_ff_3 (
    .J(and_2_out), .clk(Clock), .K(and_2_out), .Q(out_3), .reset(or_1_out));  // open: Qn, preset, en
  J_K_Flip_Flop j_k_ff_4 (
    .J(and_3_out), .clk(Clock), .K(and_3_out), .Q(out_4), .reset(or_1_out));  // open: Qn, preset, en
  and and_4 (and_4_out, out_3, out_4);
  or or_1 (or_1_out, and_4_out, and_1_out, Reset);

  // Notes on the sheet:
  //   out_5: pull=up
endmodule
